# Fritzing sketch ads1115 (saved by Fritzing 0.9.3b)
circuit board: 5.3cm x 3.5cm
breadboards: 1

parts:
  ADS1115 = Adafruit ADS1115 16Bit I2C ADC [part_number="Adafruit #1085"]
  J = female pin header, 10 pins [form="♀ (female)"]
  ADDR = female pin header, 1 pin [form="♀ (female)"]
  VDD = female pin header, 6 pins [form="♀ (female)"]
  GND = female pin header, 6 pins [form="♀ (female)"]
  SCL = female pin header, 6 pins [form="♀ (female)"]
  SDA = female pin header, 6 pins [form="♀ (female)"]

nets:
  N1: ADS1115.AIN3, J.pin10
  N2: ADS1115.AIN2, J.pin9
  N3: ADS1115.AIN1, J.pin8
  N4: ADS1115.AIN0, J.pin7
  N5: ADS1115.ALERT, J.pin6
  N6: ADS1115.ADDR, J.pin5, ADDR.pin1
  N7: ADS1115.SDA, J.pin4, SDA.pin1, SDA.pin2, SDA.pin3, SDA.pin4, SDA.pin5, SDA.pin6
  N8: ADS1115.SCL, J.pin3, SCL.pin1, SCL.pin2, SCL.pin3, SCL.pin4, SCL.pin5, SCL.pin6
  N9: ADS1115.GND, J.pin2, GND.pin1, GND.pin2, GND.pin3, GND.pin4, GND.pin5, GND.pin6
  N10: ADS1115.VDD, J.pin1, VDD.pin1, VDD.pin2, VDD.pin3, VDD.pin4, VDD.pin5, VDD.pin6

custom parts:
  Adafruit ADS1115 16Bit I2C ADC: For microcontrollers without an analog-to-digital converter or when you want a higher-precision ADC, the ADS1115 provides 16-bit precision at 860 samples/second over I2C. The chip can be configured as 4 single-ended input channels, or two differential channels. As a nice bonus, it even includes a programmable gain amplifier, up to x16, to help boost up smaller single/differential signals to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
