# Fritzing sketch all (saved by Fritzing 0.9.3b)
breadboards: 3

parts:
  S1 = SWITCH-MOMENTARY-2 [package=tactile-pth-12mm]  # not connected
  S2 = SWITCH-MOMENTARY-2 [package=tactile-pth-12mm]  # not connected
  S3 = SWITCH-MOMENTARY-2 [package=tactile-pth-12mm]  # not connected
  S4 = SWITCH-MOMENTARY-2 [package=tactile-pth-12mm]  # not connected
  S5 = SWITCH-MOMENTARY-2 [package=tactile-pth-12mm]  # not connected
  S6 = SWITCH-MOMENTARY-2 [package=tactile-pth-12mm]  # not connected
  S7 = SWITCH-MOMENTARY-2 [package=tactile-pth-12mm]  # not connected
  S8 = SWITCH-MOMENTARY-2 [package=tactile-pth-12mm]  # not connected
  S9 = SWITCH-MOMENTARY-2 [package=tactile-pth-12mm]  # not connected
  Raspberry_Pi_1 = Raspberry Pi 3 [part_number=RPI-3-V1.2]
  パーツ1 = Adafruit ADS1015 12Bit I2C ADC [part_number="Adafruit #1083"]
  IC1 = MCP23017 I2C I/O Expander
  IC2 = MCP23017 I2C I/O Expander

nets:
  VDD: Raspberry_Pi_1.3v3, パーツ1.VDD, IC1.VDD, IC1.RESET, IC2.VDD
  N1: Raspberry_Pi_1.GPIO2, パーツ1.SDA, IC1.SCL, IC2.SCL
  N2: Raspberry_Pi_1.GPIO3, パーツ1.SCL, IC1.SDA, IC2.SDA
  VSS: パーツ1.GND, IC1.VSS, IC1.A0, IC1.A1, IC1.A2, IC2.VSS

custom parts:
  Adafruit ADS1015 12Bit I2C ADC: For microcontrollers without an analog-to-digital converter or when you want a higher-precision ADC, the ADS1015 provides 12-bit precision at 3300 samples/second over I2C. The chip can be configured as 4 single-ended input channels, or two differential channels. As a nice bonus, it even includes a programmable gain amplifier, up to x16, to help boost up smaller single/differential signals to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
  MCP23017 I2C I/O Expander: The MCP23017 uses two i2c pins (these can be shared with other i2c devices), and in exchange gives you 16 general purpose pins. You can set each of 16 pins to be input, output, input with a pullup or open drain. There's even the ability to get an interrupt via an external pin when any of the inputs change so you don't have to keep polling the chip.
