# Fritzing sketch jack (saved by Fritzing 0.9.3b)
circuit board: 19cm x 7.8cm
breadboards: 1

parts:
  IC1 = MCP23017 I2C I/O Expander
  IC2 = MCP23017 I2C I/O Expander
  J_Q = BANANA_CONN [package=banana_conn]
  J_W = BANANA_CONN [package=banana_conn]
  J_E = BANANA_CONN [package=banana_conn]
  J_R = BANANA_CONN [package=banana_conn]
  J_T = BANANA_CONN [package=banana_conn]
  J_Z = BANANA_CONN [package=banana_conn]
  J_U = BANANA_CONN [package=banana_conn]
  J_I = BANANA_CONN [package=banana_conn]
  J_O = BANANA_CONN [package=banana_conn]
  J_H = BANANA_CONN [package=banana_conn]
  J_S = BANANA_CONN [package=banana_conn]
  J_F = BANANA_CONN [package=banana_conn]
  J_K = BANANA_CONN [package=banana_conn]
  J_G = BANANA_CONN [package=banana_conn]
  J_D = BANANA_CONN [package=banana_conn]
  J_A = BANANA_CONN [package=banana_conn]
  J_J = BANANA_CONN [package=banana_conn]
  J_B = BANANA_CONN [package=banana_conn]
  J_L = BANANA_CONN [package=banana_conn]
  J_Y = BANANA_CONN [package=banana_conn]
  J_C = BANANA_CONN [package=banana_conn]
  J_M = BANANA_CONN [package=banana_conn]
  J_V = BANANA_CONN [package=banana_conn]
  J_X = BANANA_CONN [package=banana_conn]
  J_P = BANANA_CONN [package=banana_conn]
  J_N = BANANA_CONN [package=banana_conn]
  J1 = female pin header, 4 pins [form="♀ (female)"]
  J3 = female pin header, 4 pins [form="♀ (female)"]
  R1 = Resistor [tolerance=±5% resistance=51k package=THT]
  R2 = Resistor [tolerance=±5% resistance=51k package=THT]
  R3 = Resistor [tolerance=±5% resistance=51k package=THT]
  R4 = Resistor [tolerance=±5% resistance=51k package=THT]
  R5 = Resistor [tolerance=±5% resistance=51k package=THT]
  R6 = Resistor [tolerance=±5% resistance=51k package=THT]
  R7 = Resistor [tolerance=±5% resistance=51k package=THT]
  R8 = Resistor [tolerance=±5% resistance=51k package=THT]
  R9 = Resistor [tolerance=±5% resistance=51k package=THT]
  R10 = Resistor [tolerance=±5% resistance=51k package=THT]
  R11 = Resistor [tolerance=±5% resistance=51k package=THT]
  R12 = Resistor [tolerance=±5% resistance=51k package=THT]
  R13 = Resistor [tolerance=±5% resistance=51k package=THT]
  R14 = Resistor [tolerance=±5% resistance=51k package=THT]
  R15 = Resistor [tolerance=±5% resistance=51k package=THT]
  R16 = Resistor [tolerance=±5% resistance=51k package=THT]
  R17 = Resistor [tolerance=±5% resistance=51k package=THT]
  R18 = Resistor [tolerance=±5% resistance=51k package=THT]
  R19 = Resistor [tolerance=±5% resistance=51k package=THT]
  R20 = Resistor [tolerance=±5% resistance=51k package=THT]
  R21 = Resistor [tolerance=±5% resistance=51k package=THT]
  R22 = Resistor [tolerance=±5% resistance=51k package=THT]
  R23 = Resistor [tolerance=±5% resistance=51k package=THT]
  R24 = Resistor [tolerance=±5% resistance=51k package=THT]
  R25 = Resistor [tolerance=±5% resistance=51k package=THT]
  R26 = Resistor [tolerance=±5% resistance=51k package=THT]

nets:
  N1: IC1.GPB0, J_F.1, R13.Pin_1
  N2: IC1.GPB1, J_D.1, R12.Pin_1
  N3: IC1.GPB2, J_S.1, R11.Pin_1
  N4: IC1.GPB3, J_A.1, R10.Pin_1
  N5: IC1.GPB4, J_C.1, R17.Pin_1
  N6: IC1.GPB5, J_X.1, R16.Pin_1
  N7: IC1.GPB6, J_Y.1, R15.Pin_1
  N8: IC1.GPB7, J_P.1, R14.Pin_1
  N9: IC1.VDD, IC1.RESET, J1.pin1
  N10: IC1.VSS, IC1.A0, IC1.A1, IC1.A2, J1.pin2
  N11: IC1.SCL, J1.pin3
  N12: IC1.SDA, J1.pin4
  N13: IC1.GPA0, J_L.1, R26.Pin_1
  N14: IC1.GPA1, J_M.1, R25.Pin_1
  N15: IC1.GPA2, J_N.1, R24.Pin_1
  N16: IC1.GPA3, J_B.1, R23.Pin_1
  N17: IC1.GPA4, J_V.1, R22.Pin_1
  N18: IC2.GPB0, J_K.1, R21.Pin_1
  N19: IC2.GPB1, J_J.1, R20.Pin_1
  N20: IC2.GPB2, J_H.1, R19.Pin_1
  N21: IC2.GPB3, J_G.1, R18.Pin_1
  N22: IC2.GPB4, J_O.1, R9.Pin_0
  N23: IC2.GPB5, J_I.1, R8.Pin_0
  N24: IC2.GPB6, J_U.1, R7.Pin_0
  N25: IC2.GPB7, J_Z.1, R6.Pin_0
  N26: IC2.VDD, IC2.A0, IC2.RESET, J3.pin4
  N27: IC2.VSS, IC2.A1, IC2.A2, J3.pin3
  N28: IC2.SCL, J3.pin2
  N29: IC2.SDA, J3.pin1
  N30: IC2.INTB, J_T.1, R1.Pin_0
  N31: IC2.INTA, J_R.1, R2.Pin_0
  N32: IC2.GPA0, J_E.1, R3.Pin_0
  N33: IC2.GPA1, J_W.1, R4.Pin_0
  N34: IC2.GPA2, J_Q.1, R5.Pin_0

custom parts:
  MCP23017 I2C I/O Expander: The MCP23017 uses two i2c pins (these can be shared with other i2c devices), and in exchange gives you 16 general purpose pins. You can set each of 16 pins to be input, output, input with a pullup or open drain. There's even the ability to get an interrupt via an external pin when any of the inputs change so you don't have to keep polling the chip.
