# Fritzing sketch key (saved by Fritzing 0.9.3b)
circuit board: 16.5cm x 3.6cm
breadboards: 2

parts:
  S_Q = SWITCH-MOMENTARY-2 [package=tactile-pth-12mm]
  S_E = SWITCH-MOMENTARY-2 [package=tactile-pth-12mm]
  S_W = SWITCH-MOMENTARY-2 [package=tactile-pth-12mm]
  S_R = SWITCH-MOMENTARY-2 [package=tactile-pth-12mm]
  S_U = SWITCH-MOMENTARY-2 [package=tactile-pth-12mm]
  S_Y = SWITCH-MOMENTARY-2 [package=tactile-pth-12mm]
  S_T = SWITCH-MOMENTARY-2 [package=tactile-pth-12mm]
  S_I = SWITCH-MOMENTARY-2 [package=tactile-pth-12mm]
  S_O = SWITCH-MOMENTARY-2 [package=tactile-pth-12mm]
  R27 = Resistor [tolerance=±20% resistance=1k package=THT]
  R28 = Resistor [tolerance=±5% resistance=100 package=THT]
  R30 = Resistor [tolerance=±5% resistance=200 package=THT]
  R31 = Resistor [tolerance=±5% resistance=330 package=THT]
  R32 = Resistor [tolerance=±5% resistance=510 package=THT]
  R33 = Resistor [tolerance=±5% resistance=910 package=THT]
  R34 = Resistor [tolerance=±5% resistance=2k package=THT]
  R35 = Resistor [tolerance=±5% resistance=6.2k package=THT]
  R36 = Resistor [tolerance=±5% resistance=150 package=THT]
  J1 = female pin header, 3 pins [form="♀ (female)"]

nets:
  N1: S_Q.1, S_E.1, S_W.1, S_R.1, S_U.1, S_Y.1, S_T.1, S_I.1, S_O.1, R35.Pin_1, J1.pin1
  N2: S_Q.2, R27.Pin_0, J1.pin2
  N3: S_E.2, R28.Pin_1, R36.Pin_0
  N4: S_W.2, R27.Pin_1, R28.Pin_0, J1.pin3
  N5: S_R.2, R30.Pin_0, R36.Pin_1
  N6: S_U.2, R32.Pin_1, R33.Pin_0
  N7: S_Y.2, R31.Pin_1, R32.Pin_0
  N8: S_T.2, R30.Pin_1, R31.Pin_0
  N9: S_I.2, R33.Pin_1, R34.Pin_0
  N10: S_O.2, R34.Pin_1, R35.Pin_0
