# Fritzing sketch mcp23017_board (saved by Fritzing 0.9.3b)
circuit board: 5.5cm x 4.8cm

parts:
  IC1 = MCP23017 I2C I/O Expander
  J1 = female pin header, 14 pins [form="♀ (female)"]
  J2 = female pin header, 14 pins [form="♀ (female)"]
  R1 = Resistor [tolerance=±5% resistance=220 package=THT]
  R2 = Resistor [tolerance=±5% resistance=220 package=THT]
  R3 = Resistor [tolerance=±5% resistance=220 package=THT]
  R4 = Resistor [tolerance=±5% resistance=220 package=THT]
  R5 = Resistor [tolerance=±5% resistance=220 package=THT]
  R6 = Resistor [tolerance=±5% resistance=220 package=THT]
  R7 = Resistor [tolerance=±5% resistance=220 package=THT]
  R8 = Resistor [tolerance=±5% resistance=220 package=THT]
  R9 = Resistor [tolerance=±5% resistance=220 package=THT]
  R10 = Resistor [tolerance=±5% resistance=220 package=THT]
  R11 = Resistor [tolerance=±5% resistance=220 package=THT]
  R12 = Resistor [tolerance=±5% resistance=220 package=THT]
  R13 = Resistor [tolerance=±5% resistance=220 package=THT]
  R14 = Resistor [tolerance=±5% resistance=220 package=THT]
  R15 = Resistor [tolerance=±5% resistance=220 package=THT]
  R16 = Resistor [tolerance=±5% resistance=220 package=THT]
  GND = female pin header, 3 pins [form="♀ (female)"]  # not connected
  3_3v = female pin header, 3 pins [form="♀ (female)"]
  POWER = female pin header, 2 pins [form="♀ (female)"]

nets:
  N1: IC1.GPB0, J1.pin1, R16.Pin_1
  N2: IC1.GPB1, J1.pin2, R15.Pin_1
  N3: IC1.GPB2, J1.pin3, R14.Pin_1
  N4: IC1.GPB3, J1.pin4, R13.Pin_1
  N5: IC1.GPB4, J1.pin5, R12.Pin_1
  N6: IC1.GPB5, J1.pin6, R11.Pin_1
  N7: IC1.GPB6, J1.pin7, R10.Pin_1
  N8: IC1.GPB7, J1.pin8, R9.Pin_1
  N9: IC1.VDD, IC1.RESET, J1.pin9, J2.pin11, 3_3v.pin1, 3_3v.pin2, 3_3v.pin3, POWER.pin1
  N10: IC1.VSS, J1.pin10
  N11: IC1.SCL, J1.pin12
  N12: IC1.SDA, J1.pin13
  N13: IC1.A0, J2.pin14
  N14: IC1.A1, J2.pin13
  N15: IC1.A2, J2.pin12
  N16: IC1.INTB, J2.pin10
  N17: IC1.INTA, J2.pin9
  N18: IC1.GPA0, J2.pin8, R1.Pin_0
  N19: IC1.GPA1, J2.pin7, R2.Pin_0
  N20: IC1.GPA2, J2.pin6, R3.Pin_0
  N21: IC1.GPA3, J2.pin5, R4.Pin_0
  N22: IC1.GPA4, J2.pin4, R5.Pin_0
  N23: IC1.GPA5, J2.pin3, R6.Pin_0
  N24: IC1.GPA6, J2.pin2, R7.Pin_0
  N25: IC1.GPA7, J2.pin1, R8.Pin_0

custom parts:
  MCP23017 I2C I/O Expander: The MCP23017 uses two i2c pins (these can be shared with other i2c devices), and in exchange gives you 16 general purpose pins. You can set each of 16 pins to be input, output, input with a pullup or open drain. There's even the ability to get an interrupt via an external pin when any of the inputs change so you don't have to keep polling the chip.
